// Logisim project AsynchronousCounter.circ as structural Verilog: 1 circuit, main circuit main
module main (
  input  A,
  input  R,
  output Q2,
  output Q1
);

  wire Clk_out, not_1_out;

  T_Flip_Flop t_ff_1 (.T(A), .clk(Clk_out), .Q(Q2), .reset(R));  // open: Qn, preset
  Clock Clk (.out(Clk_out));
  T_Flip_Flop t_ff_2 (.T(A), .clk(not_1_out), .Q(Q1), .reset(R));  // open: Qn, preset
  not not_1 (not_1_out, Q2);
endmodule
