// Logisim project D-FF.circ as structural Verilog: 1 circuit, main circuit main
module main (
  input  in_1,
  output out_2,
  output out_3
);

  wire clock_1_out, not_1_out;

  Clock clock_1 (.out(clock_1_out));
  not not_1 (not_1_out, clock_1_out);
  Multiplexer multiplexer_1 (.in0(out_2), .in1(in_1), .out(out_2), .sel(not_1_out));
  Multiplexer multiplexer_2 (.in0(out_3), .in1(out_2), .out(out_3), .sel(clock_1_out));
endmodule
