// Logisim project LATCH.circ as structural Verilog: 1 circuit, main circuit main
module main (
  input  in_1,
  output out_2
);

  wire clock_1_out;

  Clock clock_1 (.out(clock_1_out));
  Multiplexer multiplexer_1 (.in0(out_2), .in1(in_1), .out(out_2), .sel(clock_1_out));
endmodule
