// Logisim project MUX.circ as structural Verilog: 1 circuit, main circuit main
module main (
  input  in_1,
  input  in_2,
  input  in_3,
  output out_4
);

  wire not_1_out;

  not not_1 (not_1_out, in_2);
  // Transmission_Gate transmission_1: pin names not known; wires that end beside it: in_1, in_2, not_1_out, out_4
  // Transmission_Gate transmission_2: pin names not known; wires that end beside it: in_3, not_1_out, in_2, out_4
endmodule
