// Logisim project SynchronousUPDOWNCounter.circ as structural Verilog: 1 circuit, main circuit main
module main (
  input  in_1,
  output out_2,
  output out_3,
  output out_4,
  output out_5
);

  wire adder_1_cout, adder_1_out, adder_2_cout, adder_2_out, adder_3_cout, adder_3_out, adder_4_out,
       clock_1_out, not_1_out;

  Clock clock_1 (.out(clock_1_out));
  Adder #(.width(1)) adder_1 (.a(1'b1), .b(out_2), .out(adder_1_out), .cout(adder_1_cout));  // open: cin
  D_Flip_Flop d_ff_1 (.D(adder_1_out), .clk(clock_1_out), .Q(out_2));  // open: Qn, preset, reset
  not not_1 (not_1_out, in_1);
  D_Flip_Flop d_ff_2 (.D(adder_2_out), .clk(clock_1_out), .Q(out_3));  // open: Qn, preset, reset
  Adder #(.width(1)) adder_2 (.a(not_1_out), .b(out_3), .out(adder_2_out), .cin(adder_1_cout), .cout(adder_2_cout));
  Adder #(.width(1)) adder_3 (.a(not_1_out), .b(out_4), .out(adder_3_out), .cin(adder_2_cout), .cout(adder_3_cout));
  D_Flip_Flop d_ff_3 (.D(adder_3_out), .clk(clock_1_out), .Q(out_4));  // open: Qn, preset, reset
  Adder #(.width(1)) adder_4 (.a(not_1_out), .b(out_5), .out(adder_4_out), .cin(adder_3_cout));  // open: cout
  D_Flip_Flop d_ff_4 (.D(adder_4_out), .clk(clock_1_out), .Q(out_5));  // open: Qn, preset, reset
endmodule
